# Fritzing sketch RGB_funzionante (saved by Fritzing 0.9.3b)
breadboards: 1

parts:
  Digispark1 = Digispark
  S1 = Pushbutton [package="[THT]"]
  S2 = Pushbutton [package="[THT]"]
  S3 = Pushbutton [package="[THT]"]
  LED1 = RGB LED (com. anode, rbg) [package="5 mm [THT]"]
  R1 = Resistor [tolerance=±5% resistance=220 package="0603 [SMD]"]
  R2 = Resistor [tolerance=±5% resistance=220 package="0603 [SMD]"]
  R3 = Resistor [tolerance=±5% resistance=220 package="0603 [SMD]"]
  R4 = Resistor [tolerance=±5% resistance=220 package="0603 [SMD]"]
  R5 = Resistor [tolerance=±5% resistance=220 package="0603 [SMD]"]
  R6 = Resistor [tolerance=±5% resistance=220 package="0603 [SMD]"]

nets:
  N1: Digispark1.VCC, S1.Pin_3, S1.Pin_4, S2.Pin_3, S2.Pin_4, S3.Pin_3, S3.Pin_4
  N2: Digispark1.GND, LED1.common_anode, R1.Pin_1, R2.Pin_1, R3.Pin_1
  N3: Digispark1.P0, R4.Pin_1
  N4: Digispark1.P1, R5.Pin_1
  N5: Digispark1.P2, S1.Pin_1, S1.Pin_2, R1.Pin_0
  N6: Digispark1.P3, S2.Pin_1, S2.Pin_2, R2.Pin_0
  N7: Digispark1.P4, R6.Pin_1
  N8: Digispark1.P5, S3.Pin_1, S3.Pin_2, R3.Pin_0
  N9: LED1.red_cathode, R4.Pin_0
  N10: LED1.blue_cathode, R5.Pin_0
  N11: LED1.green_cathode, R6.Pin_0

custom parts:
  Digispark: The Digispark is an Attiny85 based microcontroller development board similar to the Arduino line, only cheaper, smaller, and a bit less powerful. With a whole host of shields to extend its functionality and the ability to use the familiar Arduino IDE the Digispark is a great way to jump into electronics, or perfect for when an Arduino is too big or too much.
