# Fritzing sketch Schema_RGB_Button (saved by Fritzing 0.9.3b)
breadboards: 1

parts:
  R1 = Resistor [tolerance=±5% resistance=220 package="0603 [SMD]"]
  R2 = Resistor [tolerance=±5% resistance=220 package="0805 [SMD]"]
  R3 = Resistor [tolerance=±5% resistance=220 package="0805 [SMD]"]
  LED1 = RGB LED (com. cathode, rbg) [package="5 mm [THT]"]
  S1 = Pushbutton [package="[SMD]"]
  Digispark1 = Digispark
  R4 = Resistor [tolerance=±5% resistance=220 package="0603 [SMD]"]

nets:
  N1: R1.Pin_0, LED1.red_anode, Digispark1.P4
  N2: R1.Pin_1, R2.Pin_1, R3.Pin_1, S1.Pin_1, S1.Pin_2, Digispark1.VCC, Digispark1.P5
  N3: R2.Pin_0, LED1.blue_anode, Digispark1.P0
  N4: R3.Pin_0, LED1.green_anode, Digispark1.P1
  N5: LED1.common_cathode, Digispark1.GND, R4.Pin_1
  N6: S1.Pin_3, S1.Pin_4, R4.Pin_0

custom parts:
  Digispark: The Digispark is an Attiny85 based microcontroller development board similar to the Arduino line, only cheaper, smaller, and a bit less powerful. With a whole host of shields to extend its functionality and the ability to use the familiar Arduino IDE the Digispark is a great way to jump into electronics, or perfect for when an Arduino is too big or too much.
